# Fritzing sketch Assigment2 sensor (saved by Fritzing 0.9.3b)
breadboards: 2

parts:
  Part1 = HC-SR04
  DHT1 = DHT11 Humitidy and Temperature Sensor
  Mod1 = NodeMCU V1.0
  A1 = 1 chan 3v relay module

nets:
  N1: Part1.Vcc, A1.pin_1
  N2: Part1.Trig, Mod1.D6
  N3: Part1.Echo, Mod1.D5
  GND: Part1.Gnd, DHT1.GND, Mod1.GND, A1.pin_3
  VDD: DHT1.VDD, Mod1.3V3
  N4: DHT1.DATA, Mod1.D4
  N5: Mod1.D0, A1.pin_2

custom parts:
  HC-SR04: HC-SR04 ultrasonic distance sensor
  DHT11 Humitidy and Temperature Sensor: DHT11 Humidity and Temperature Sensor
  NodeMCU V1.0: ESP8266 based NodeMCU
  1 chan 3v relay module: Single 3V relay isolated drive control module High level drive board.
